// Logisim project 4bitComputer.circ as structural Verilog: 17 circuits, main circuit 4bitkaydedici
module _4bitkaydedici (
  input  INC,
  input  ld,
  input  [3:0] INPUT,
  input  CLK,
  input  CLR,
  output [3:0] OUTPUT
);

  wire and_1_out, and_2_out, and_3_out, and_4_out, and_5_out, and_6_out, and_7_out, and_8_out, and_9_out,
       and_10_out, and_11_out, and_12_out, not_1_out, not_2_out, not_3_out, not_4_out, not_5_out, not_6_out,
       or_1_out, or_2_out, or_3_out, or_4_out, or_5_out, or_6_out, or_7_out, or_8_out;

  not not_1 (not_1_out, ld);
  and and_1 (and_1_out, INC, not_1_out);
  not not_2 (not_2_out, not_1_out);
  not not_3 (not_3_out, INPUT[0]);
  not not_4 (not_4_out, INPUT[1]);
  not not_5 (not_5_out, INPUT[2]);
  not not_6 (not_6_out, INPUT[3]);
  and and_2 (and_2_out, not_2_out, INPUT[0]);
  and and_3 (and_3_out, not_2_out, not_3_out);
  and and_4 (and_4_out, not_2_out, INPUT[1]);
  and and_5 (and_5_out, not_2_out, not_4_out);
  and and_6 (and_6_out, not_2_out, INPUT[2]);
  and and_7 (and_7_out, not_2_out, not_5_out);
  and and_8 (and_8_out, not_2_out, INPUT[3]);
  and and_9 (and_9_out, not_2_out, not_6_out);
  and and_10 (and_10_out, and_1_out, OUTPUT[0]);
  and and_11 (and_11_out, and_1_out, OUTPUT[0], OUTPUT[1]);
  and and_12 (and_12_out, and_1_out, OUTPUT[0], OUTPUT[1], OUTPUT[2]);
  or or_1 (or_1_out, and_2_out, and_1_out);
  or or_2 (or_2_out, and_3_out, and_1_out);
  or or_3 (or_3_out, and_4_out, and_10_out);
  or or_4 (or_4_out, and_10_out, and_5_out);
  or or_5 (or_5_out, and_6_out, and_11_out);
  or or_6 (or_6_out, and_11_out, and_7_out);
  or or_7 (or_7_out, and_8_out, and_12_out);
  or or_8 (or_8_out, and_12_out, and_9_out);
  J_K_Flip_Flop j_k_ff_1 (.J(or_1_out), .clk(CLK), .K(or_2_out), .Q(OUTPUT[0]), .reset(CLR));  // open: Qn, preset, en
  J_K_Flip_Flop j_k_ff_2 (.J(or_3_out), .clk(CLK), .K(or_4_out), .Q(OUTPUT[1]), .reset(CLR));  // open: Qn, preset, en
  J_K_Flip_Flop j_k_ff_3 (.J(or_5_out), .clk(CLK), .K(or_6_out), .Q(OUTPUT[2]), .reset(CLR));  // open: Qn, preset, en
  J_K_Flip_Flop j_k_ff_4 (.J(or_7_out), .clk(CLK), .K(or_8_out), .Q(OUTPUT[3]), .reset(CLR));  // open: Qn, preset, en
endmodule

module _8_bitlik_reg (
  input  [7:0] INPUT,
  input  in_2,
  input  CLK,
  output [7:0] out_4
);

  _4bitkaydedici u_4bitkaydedici_1 (.INPUT(INPUT[3:0]), .CLK(CLK), .ld(in_2), .OUTPUT(out_4[3:0]));  // open: INC, CLR
  _4bitkaydedici u_4bitkaydedici_2 (.INPUT(INPUT[7:4]), .CLK(CLK), .ld(in_2), .OUTPUT(out_4[7:4]));  // open: INC, CLR
endmodule

module main (
);

  wire and_1_out, clock_1_out, control_unit_1_dr_bus, control_unit_1_hlt, control_unit_1_outr__ld;
  wire [1:0] control_unit_1_ir_bus, control_unit_1_m___bus;
  wire [2:0] control_unit_1_ar_bus, control_unit_1_pc_bus;
  wire [3:0] AC_output, alu_4_1_out_14, AR_output, control_unit_1_ac_bus, controlled_buffer_1_out,
       controlled_buffer_1_out_2, DR_output, INPR_output, IR_out_4, IR_out_4_2, OUTR_output, PC_output;
  wire [6:0] control_unit_1_and;
  wire [7:0] ram_1_data;

  Control_Unit control_unit_1 (
    .IR(IR_out_4_2), .CLK(and_1_out), .HLT(control_unit_1_hlt), .M___BUS(control_unit_1_m___bus),
    .AR_BUS(control_unit_1_ar_bus), .PC_BUS(control_unit_1_pc_bus), .DR_BUS(control_unit_1_dr_bus),
    .AC_BUS(control_unit_1_ac_bus), .IR_BUS(control_unit_1_ir_bus), .OUTR__LD(control_unit_1_outr__ld),
    .AND(control_unit_1_and[0]), .ADD(control_unit_1_and[1]), .LD_DR(control_unit_1_and[2]),
    .COMP(control_unit_1_and[3]), .LD_INPR(control_unit_1_and[4]), .CIR(control_unit_1_and[5]),
    .CIL(control_unit_1_and[6]));  // open: E
  and and_1 (and_1_out, ~control_unit_1_hlt, clock_1_out);  // AND_Gate
  ALU_4 alu_4_1 (
    .AC(AC_output), .DR(DR_output), .INPR(INPR_output), .AND(control_unit_1_and[0]),
    .ADD(control_unit_1_and[1]), .LD_DR(control_unit_1_and[2]), .COMP(control_unit_1_and[3]),
    .LD_INPR(control_unit_1_and[4]), .CIR(control_unit_1_and[5]), .CIL(control_unit_1_and[6]),
    .out_14(alu_4_1_out_14));  // open: E_AC_0, cin, E_AC_3, cout
  RAM #(.addrWidth(4), .bus("separate")) ram_1 (
    .addr(AR_output), .din({controlled_buffer_1_out_2, controlled_buffer_1_out}), .data(ram_1_data),
    .str(control_unit_1_m___bus[0]), .clk(and_1_out));  // open: sel, ld, clr
  // Probe on AR_output
  _4bitkaydedici AR (
    .INPUT(controlled_buffer_1_out), .CLK(and_1_out), .ld(control_unit_1_ar_bus[0]),
    .INC(control_unit_1_ar_bus[1]), .OUTPUT(AR_output));  // open: CLR
  // Probe on PC_output
  _4bitkaydedici PC (
    .INPUT(controlled_buffer_1_out), .CLK(and_1_out), .ld(control_unit_1_pc_bus[0]),
    .INC(control_unit_1_pc_bus[1]), .OUTPUT(PC_output));  // open: CLR
  // Probe on DR_output
  _4bitkaydedici DR (
    .INPUT(controlled_buffer_1_out), .CLK(and_1_out), .ld(control_unit_1_dr_bus), .OUTPUT(DR_output));  // open: INC, CLR
  // Probe on AC_output
  _4bitkaydedici AC (
    .INPUT(alu_4_1_out_14), .CLK(and_1_out), .ld(control_unit_1_ac_bus[0]), .INC(control_unit_1_ac_bus[1]),
    .CLR(control_unit_1_ac_bus[2]), .OUTPUT(AC_output));
  // Probe on INPR_output
  _4bitkaydedici INPR (.OUTPUT(INPR_output));  // open: INPUT, CLK, ld, INC, CLR
  // Probe on {IR_out_4_2, IR_out_4}
  _8_bitlik_reg IR (
    .INPUT({controlled_buffer_1_out_2, controlled_buffer_1_out}), .CLK(and_1_out),
    .in_2(control_unit_1_ir_bus[0]), .out_4({IR_out_4_2, IR_out_4}));
  // Probe on OUTR_output
  _4bitkaydedici OUTR (
    .INPUT(controlled_buffer_1_out), .CLK(and_1_out), .ld(control_unit_1_outr__ld), .OUTPUT(OUTR_output));  // open: INC, CLR
  assign {controlled_buffer_1_out_2, controlled_buffer_1_out} = control_unit_1_m___bus[1] ? ram_1_data : 8'bz;  // Controlled_Buffer controlled_buffer_1
  assign {controlled_buffer_1_out_2, controlled_buffer_1_out} = control_unit_1_ar_bus[2] ? {4'b0000, AR_output} : 8'bz;  // Controlled_Buffer controlled_buffer_2
  assign {controlled_buffer_1_out_2, controlled_buffer_1_out} = control_unit_1_pc_bus[2] ? {4'b0000, PC_output} : 8'bz;  // Controlled_Buffer controlled_buffer_3
  assign {controlled_buffer_1_out_2, controlled_buffer_1_out} = control_unit_1_ac_bus[3] ? {4'b0000, AC_output} : 8'bz;  // Controlled_Buffer controlled_buffer_4
  assign {controlled_buffer_1_out_2, controlled_buffer_1_out} = control_unit_1_ir_bus[1] ? {IR_out_4_2, IR_out_4} : 8'bz;  // Controlled_Buffer controlled_buffer_5
  Clock clock_1 (.out(clock_1_out));
endmodule

// main Control
module Control_Unit (
  input  [3:0] IR,
  input  CLK,
  output [1:0] M___BUS,
  output [2:0] AR_BUS,
  output [2:0] PC_BUS,
  output DR_BUS,
  output [3:0] AC_BUS,
  output [1:0] IR_BUS,
  output OUTR__LD,
  output AND,
  output ADD,
  output LD_DR,
  output COMP,
  output LD_INPR,
  output CIR,
  output CIL,
  output HLT,
  output E
);

  wire d_ff_1_q, decoder_1_out15, sclr_control_1_sc_clear;
  wire [1:0] decoder_2_out3;
  wire [2:0] decoder_2_out0;
  wire [3:0] counter_1_out_3;
  wire [14:0] decoder_1_out3;

  SCLR_Control sclr_control_1 (
    .T3(decoder_2_out3[0]), .T4(decoder_2_out3[1]), .D14(decoder_1_out3[14]), .D13(decoder_1_out3[13]),
    .D12(decoder_1_out3[12]), .D11(decoder_1_out3[11]), .D10(decoder_1_out3[10]), .D9(decoder_1_out3[9]),
    .D8(decoder_1_out3[8]), .D7(decoder_1_out3[7]), .D6(decoder_1_out3[6]), .D5(decoder_1_out3[5]),
    .D4(decoder_1_out3[4]), .D3(decoder_1_out3[3]), .D2(decoder_1_out3[2]), .D1(decoder_1_out3[1]),
    .D0(decoder_1_out3[0]), .SC_Clear(sclr_control_1_sc_clear));
  D_Flip_Flop d_ff_1 (.clk(CLK), .D(sclr_control_1_sc_clear), .Q(d_ff_1_q));  // open: Qn, preset, en, reset
  Counter counter_1 (.CLK(CLK), .SC_Clear(d_ff_1_q), .out_3(counter_1_out_3));
  Decoder #(.select(4)) decoder_1 (
    .out0(decoder_1_out3[0]), .out1(decoder_1_out3[1]), .out2(decoder_1_out3[2]), .out3(decoder_1_out3[3]),
    .out4(decoder_1_out3[4]), .out5(decoder_1_out3[5]), .out6(decoder_1_out3[6]), .out7(decoder_1_out3[7]),
    .out8(decoder_1_out3[8]), .out9(decoder_1_out3[9]), .out10(decoder_1_out3[10]),
    .out11(decoder_1_out3[11]), .out12(decoder_1_out3[12]), .out13(decoder_1_out3[13]),
    .out14(decoder_1_out3[14]), .out15(decoder_1_out15), .sel(IR));  // open: en
  Decoder #(.select(4)) decoder_2 (
    .out0(decoder_2_out0[0]), .out1(decoder_2_out0[1]), .out2(decoder_2_out0[2]), .out3(decoder_2_out3[0]),
    .out4(decoder_2_out3[1]), .sel(counter_1_out_3));  // open: out5, out6, out7, out8, out9, out10, out11, out12, out13, out14, out15, en
  and and_1 (HLT, decoder_1_out15, decoder_2_out3[0]);
  and and_2 (E, decoder_2_out3[0], decoder_1_out3[8]);
  Register_Control register_control_1 (
    .T0(decoder_2_out0[0]), .T1(decoder_2_out0[1]), .T2(decoder_2_out0[2]), .T3(decoder_2_out3[0]),
    .T4(decoder_2_out3[1]), .D14(decoder_1_out3[14]), .D13(decoder_1_out3[13]), .D12(decoder_1_out3[12]),
    .D11(decoder_1_out3[11]), .D10(decoder_1_out3[10]), .D9(decoder_1_out3[9]), .D8(decoder_1_out3[8]),
    .D7(decoder_1_out3[7]), .D6(decoder_1_out3[6]), .D5(decoder_1_out3[5]), .D4(decoder_1_out3[4]),
    .D3(decoder_1_out3[3]), .D2(decoder_1_out3[2]), .D1(decoder_1_out3[1]), .D0(decoder_1_out3[0]),
    .M___BUS(M___BUS), .AR_BUS(AR_BUS), .PC_BUS(PC_BUS), .DR_BUS(DR_BUS), .AC_BUS(AC_BUS), .IR_BUS(IR_BUS),
    .OUTR__LD(OUTR__LD));
  ALU_Control alu_control_1 (
    .T3(decoder_2_out3[0]), .T4(decoder_2_out3[1]), .D0(decoder_1_out3[0]), .D1(decoder_1_out3[1]),
    .D2(decoder_1_out3[2]), .D9(decoder_1_out3[9]), .D11(decoder_1_out3[11]), .D12(decoder_1_out3[12]),
    .D13(decoder_1_out3[13]), .AND(AND), .ADD(ADD), .LD_DR(LD_DR), .COMP(COMP), .LD_INPR(LD_INPR), .CIR(CIR),
    .CIL(CIL));

  // Notes on the sheet:
  //   SC Clear
  //   D(0_15)
  //   T(0_4)
  //   Counter
  //   Register Control
  //   ALU Control
endmodule

module ALU_1 (
  input  INPR,
  input  DR,
  input  AC,
  input  AND,
  input  ADD,
  input  cin,
  input  ld_DR,
  input  COMP,
  input  ld_INPR,
  input  SHR,
  input  SHL,
  input  AC_i_1,
  input  AC_i_1_2,
  output cout,
  output Output_AC
);

  wire add_out, adder_1_out, and_1_out, and_2_out, comp_out, ld_DR_out, ld_INPR_out, not_1_out, SHL_out,
       SHR_out;

  and and_1 (and_1_out, AC, DR);
  Adder #(.width(1)) adder_1 (.a(AC), .b(DR), .out(adder_1_out), .cin(cin), .cout(cout));
  not not_1 (not_1_out, AC);
  and and_2 (and_2_out, AND, and_1_out);
  and u_add (add_out, ADD, adder_1_out);
  and u_ld_DR (ld_DR_out, ld_DR, DR);
  and u_comp (comp_out, COMP, not_1_out);
  and u_ld_INPR (ld_INPR_out, ld_INPR, INPR);
  and u_SHR (SHR_out, SHR, AC_i_1_2);
  and u_SHL (SHL_out, SHL, AC_i_1);
  or or_1 (Output_AC, and_2_out, add_out, ld_DR_out, comp_out, ld_INPR_out, SHR_out, SHL_out);
endmodule

// ALU
module ALU_4 (
  input  E_AC_0,
  input  cin,
  input  [3:0] AC,
  input  [3:0] DR,
  input  [3:0] INPR,
  input  AND,
  input  ADD,
  input  LD_DR,
  input  COMP,
  input  LD_INPR,
  input  CIR,
  input  CIL,
  input  E_AC_3,
  output [3:0] out_14,
  output cout
);

  wire alu_1_1_cout, alu_1_2_cout, alu_1_3_cout;

  ALU_1 alu_1_1 (
    .AND(AND), .ADD(ADD), .ld_DR(LD_DR), .COMP(COMP), .ld_INPR(LD_INPR), .SHR(CIR), .SHL(CIL),
    .AC_i_1(E_AC_0), .AC_i_1_2(AC[1]), .INPR(INPR[0]), .DR(DR[0]), .AC(AC[0]), .cin(cin),
    .cout(alu_1_1_cout), .Output_AC(out_14[0]));
  ALU_1 alu_1_2 (
    .AND(AND), .ADD(ADD), .ld_DR(LD_DR), .COMP(COMP), .ld_INPR(LD_INPR), .SHR(CIR), .SHL(CIL),
    .AC_i_1(AC[0]), .AC_i_1_2(AC[2]), .INPR(INPR[1]), .DR(DR[1]), .AC(AC[1]), .cin(alu_1_1_cout),
    .cout(alu_1_2_cout), .Output_AC(out_14[1]));
  ALU_1 alu_1_3 (
    .AND(AND), .ADD(ADD), .ld_DR(LD_DR), .COMP(COMP), .ld_INPR(LD_INPR), .SHR(CIR), .SHL(CIL),
    .AC_i_1(AC[1]), .AC_i_1_2(AC[3]), .INPR(INPR[2]), .DR(DR[2]), .AC(AC[2]), .cin(alu_1_2_cout),
    .cout(alu_1_3_cout), .Output_AC(out_14[2]));
  ALU_1 alu_1_4 (
    .AND(AND), .ADD(ADD), .ld_DR(LD_DR), .COMP(COMP), .ld_INPR(LD_INPR), .SHR(CIR), .SHL(CIL),
    .AC_i_1(AC[2]), .AC_i_1_2(E_AC_3), .INPR(INPR[3]), .DR(DR[3]), .AC(AC[3]), .cin(alu_1_3_cout),
    .cout(cout), .Output_AC(out_14[3]));

  // Notes on the sheet:
  //   AC(0)
  //   AC(1)
  //   AC(2)
  //   AC(3)
endmodule

module Register_Control (
  input  T0,
  input  T1,
  input  T2,
  input  T3,
  input  T4,
  input  D14,
  input  D13,
  input  D12,
  input  D11,
  input  D10,
  input  D9,
  input  D8,
  input  D7,
  input  D6,
  input  D5,
  input  D4,
  input  D3,
  input  D2,
  input  D1,
  input  D0,
  output [1:0] M___BUS,
  output [2:0] AR_BUS,
  output [2:0] PC_BUS,
  output DR_BUS,
  output [3:0] AC_BUS,
  output [1:0] IR_BUS,
  output OUTR__LD
);

  AR_Control ar_control_1 (
    .T0(T0), .T2(T2), .T3(T3), .T4(T4), .D4(D4), .D5(D5), .AR_LD(AR_BUS[0]), .AR_INC(AR_BUS[1]),
    .AR_BUS(AR_BUS[2]));
  DR dr_1 (.T3(T3), .D0(D0), .D1(D1), .D2(D2), .DR_LD(DR_BUS));
  IR ir_1 (.T1(T1), .T2(T2), .IR_LD(IR_BUS[0]), .IR_BUS(IR_BUS[1]));
  OUTR outr_1 (.T3(T3), .D14(D14), .OUTR_LD(OUTR__LD));
  Memory memory_1 (
    .T1(T1), .T3(T3), .D0(D0), .D1(D1), .D2(D2), .D3(D3), .D5(D5), .D6(D6), .Memory_STR(M___BUS[0]),
    .Memory_BUS(M___BUS[1]));
  PC_Control pc_control_1 (
    .T0(T0), .T1(T1), .T3(T3), .T4(T4), .D4(D4), .D5(D5), .D6(D6), .PC_LD(PC_BUS[0]), .PC_INC(PC_BUS[1]),
    .PC_BUS(PC_BUS[2]));
  AC ac_1 (
    .T3(T3), .T4(T4), .D0(D0), .D1(D1), .D2(D2), .D3(D3), .D7(D7), .D9(D9), .D10(D10), .D11(D11), .D12(D12),
    .D13(D13), .D14(D14), .AC_LD(AC_BUS[0]), .AC_INC(AC_BUS[1]), .AC_CLR(AC_BUS[2]), .AC_BUS(AC_BUS[3]));

  // Notes on the sheet:
  //   Memory
  //   AR
  //   PC
  //   DR
  //   AC
  //   IR
  //   OUTR
endmodule

module AR_Control (
  input  T0,
  input  T2,
  input  T3,
  input  T4,
  input  D4,
  input  D5,
  output AR_LD,
  output AR_INC,
  output AR_BUS
);

  wire and_1_out, and_2_out;

  and and_1 (and_1_out, T3, D4);
  and and_2 (and_2_out, T4, D5);
  and and_3 (AR_INC, T3, D5);
  or or_1 (AR_LD, T2, T0);
  or or_2 (AR_BUS, and_2_out, and_1_out);
endmodule

module Memory (
  input  T1,
  input  T3,
  input  D0,
  input  D1,
  input  D2,
  input  D3,
  input  D5,
  input  D6,
  output Memory_STR,
  output Memory_BUS
);

  wire and_1_out, and_2_out, and_3_out, and_4_out, and_5_out, and_6_out;

  and and_1 (and_1_out, T3, D0);
  and and_2 (and_2_out, T3, D1);
  and and_3 (and_3_out, T3, D2);
  and and_4 (and_4_out, T3, D3);
  and and_5 (and_5_out, T3, D5);
  and and_6 (and_6_out, T3, D6);
  or or_1 (Memory_STR, and_5_out, and_4_out);
  or or_2 (Memory_BUS, and_3_out, and_2_out, and_6_out, and_1_out, T1);
endmodule

module PC_Control (
  input  T0,
  input  T1,
  input  T3,
  input  T4,
  input  D4,
  input  D5,
  input  D6,
  output PC_LD,
  output PC_INC,
  output PC_BUS
);

  wire and_1_out, and_2_out, and_3_out, and_4_out;

  and and_1 (and_1_out, T3, D4);
  and and_2 (and_2_out, T4, D5);
  and and_3 (and_3_out, T3, D5);
  and and_4 (and_4_out, T3, D6);
  or or_1 (PC_LD, and_2_out, and_4_out, and_1_out);
  or or_2 (PC_BUS, and_3_out, T0);

  assign PC_INC = T1;
endmodule

module DR (
  input  T3,
  input  D0,
  input  D1,
  input  D2,
  output DR_LD
);

  wire and_1_out, and_2_out, and_3_out;

  and and_1 (and_1_out, T3, D0);
  and and_2 (and_2_out, T3, D1);
  and and_3 (and_3_out, T3, D2);
  or or_1 (DR_LD, and_2_out, and_3_out, and_1_out);
endmodule

module AC (
  input  T3,
  input  T4,
  input  D0,
  input  D1,
  input  D2,
  input  D3,
  input  D7,
  input  D9,
  input  D10,
  input  D11,
  input  D12,
  input  D13,
  input  D14,
  output AC_LD,
  output AC_INC,
  output AC_CLR,
  output AC_BUS
);

  wire and_1_out, and_2_out, and_3_out, and_4_out, and_6_out, and_7_out, and_9_out, and_10_out, and_11_out;

  and and_1 (and_1_out, T4, D0);
  and and_2 (and_2_out, T4, D1);
  and and_3 (and_3_out, T4, D2);
  and and_4 (and_4_out, T3, D3);
  and and_5 (AC_CLR, T3, D7);
  and and_6 (and_6_out, T3, D9);
  and and_7 (and_7_out, T3, D11);
  and and_8 (AC_INC, T3, D10);
  and and_9 (and_9_out, T3, D12);
  and and_10 (and_10_out, T3, D13);
  and and_11 (and_11_out, T3, D14);
  or or_1 (AC_LD, and_9_out, and_7_out, and_6_out, and_10_out, and_3_out, and_2_out, and_1_out);
  or or_2 (AC_BUS, and_11_out, and_4_out);
endmodule

module OUTR (
  input  T3,
  input  D14,
  output OUTR_LD
);

  and and_1 (OUTR_LD, T3, D14);
endmodule

module IR (
  input  T1,
  input  T2,
  output IR_LD,
  output IR_BUS
);


  assign IR_BUS = T2;
  assign IR_LD = T1;
endmodule

module ALU_Control (
  input  T3,
  input  T4,
  input  D0,
  input  D1,
  input  D2,
  input  D9,
  input  D11,
  input  D12,
  input  D13,
  output AND,
  output ADD,
  output LD_DR,
  output COMP,
  output LD_INPR,
  output CIR,
  output CIL
);

  and and_1 (AND, T4, D0);
  and and_2 (ADD, T4, D1);
  and and_3 (LD_DR, T4, D2);
  and and_4 (COMP, T3, D9);
  and and_5 (LD_INPR, T3, D13);
  and and_6 (CIR, T3, D11);
  and and_7 (CIL, T3, D12);
endmodule

module SCLR_Control (
  input  T3,
  input  T4,
  input  D14,
  input  D13,
  input  D12,
  input  D11,
  input  D10,
  input  D9,
  input  D8,
  input  D7,
  input  D6,
  input  D5,
  input  D4,
  input  D3,
  input  D2,
  input  D1,
  input  D0,
  output SC_Clear
);

  wire and_1_out, and_2_out, and_3_out, and_4_out, and_5_out, and_6_out, and_7_out, and_8_out, and_9_out,
       and_10_out, and_11_out, and_12_out, and_13_out, and_14_out, and_15_out;

  and and_1 (and_1_out, T4, D0);
  and and_2 (and_2_out, T4, D1);
  and and_3 (and_3_out, T4, D2);
  and and_4 (and_4_out, T3, D3);
  and and_5 (and_5_out, T3, D4);
  and and_6 (and_6_out, T3, D6);
  and and_7 (and_7_out, T4, D5);
  and and_8 (and_8_out, T3, D7);
  and and_9 (and_9_out, T3, D8);
  and and_10 (and_10_out, T3, D9);
  and and_11 (and_11_out, T3, D11);
  and and_12 (and_12_out, T3, D10);
  and and_13 (and_13_out, T3, D12);
  and and_14 (and_14_out, T3, D13);
  and and_15 (and_15_out, T3, D14);
  or or_1 (SC_Clear, and_1_out, and_2_out, and_3_out, and_4_out, and_5_out, and_7_out, and_6_out, and_8_out, and_9_out, and_10_out, and_12_out, and_11_out, and_13_out, and_14_out, and_15_out);
endmodule

module Counter (
  input  CLK,
  input  SC_Clear,
  output [3:0] out_3
);

  wire d_ff_1_qn, d_ff_2_qn, d_ff_3_qn, d_ff_4_qn;

  D_Flip_Flop d_ff_1 (.clk(CLK), .D(d_ff_1_qn), .Q(out_3[0]), .Qn(d_ff_1_qn), .reset(SC_Clear));  // open: preset, en
  D_Flip_Flop d_ff_2 (
    .clk(d_ff_1_qn), .D(d_ff_2_qn), .Q(out_3[1]), .Qn(d_ff_2_qn), .reset(SC_Clear));  // open: preset, en
  D_Flip_Flop d_ff_3 (
    .clk(d_ff_2_qn), .D(d_ff_3_qn), .Q(out_3[2]), .Qn(d_ff_3_qn), .reset(SC_Clear));  // open: preset, en
  D_Flip_Flop d_ff_4 (
    .clk(d_ff_3_qn), .D(d_ff_4_qn), .Q(out_3[3]), .Qn(d_ff_4_qn), .reset(SC_Clear));  // open: preset, en
endmodule
